# Fritzing sketch smart-outlet (saved by Fritzing 0.9.3b)
breadboards: 1

parts:
  KY-1 = Keyes Relay [package=THT]
  Part1 = Arduino Nano (Rev3.0)
  Part2 = NRF24L01+ Breakout Board
  Power_plug1 = Power plug
  R1 = Resistor [tolerance=±5% resistance=220 package=THT]
  LED1 = LED - 5mm [color="Red (633nm)" package="5 mm [THT]"]
  LED2 = LED - 5mm [color="Red (633nm)" package="5 mm [THT]"]
  S1 = Pushbutton [package="[THT]"]

nets:
  N1: KY-1.signal, Part1.D3
  GND: KY-1.ground, Part1.GND, Part2.GND, LED1.cathode, S1.Pin_1, S1.Pin_2
  N2: KY-1.C, LED2.anode
  N3: KY-1.NO, Power_plug1.VCC
  N4: Part1.D2, Part2.IRQ
  N5: Part1.D4, R1.Pin_0
  N6: Part1.D5, S1.Pin_3, S1.Pin_4
  N7: Part1.D9, Part2.CE
  N8: Part1.D10, Part2.CS
  N9: Part1.D11/MOSI, Part2.MOSI
  N10: Part1.D12/MISO, Part2.MISO
  3V3: Part1.3V3, Part2.VCC
  N11: Part1.D13/SCK, Part2.SCK
  N12: Power_plug1.GND, LED2.cathode
  N13: R1.Pin_1, LED1.anode

notes:
  This LED is used as a 240V example.

custom parts:
  Keyes Relay: The Keyes 5V relay module is suitable for SCM development, home appliance control. It uses a 5V~12V TIL control signal which can control DC / AC signal.
